# Fritzing sketch portasensores2 (saved by Fritzing 0.9.3b)
circuit board: 6.37732cm x 2.58708cm
breadboards: 1

parts:
  LED1 = Super Flux LED blue [color=Blue]
  LED2 = Super Flux LED blue [color=Blue]
  LED4 = Super Flux LED blue [color=Blue]
  R2 = Resistor [tolerance=±5% resistance=220 package=THT]
  R4 = Resistor [tolerance=±5% resistance=220 package=THT]
  R5 = Resistor [tolerance=±5% resistance=220 package=THT]
  R8 = Resistor [tolerance=±5% resistance=220 package=THT]
  R9 = Resistor [tolerance=±5% resistance=220 package=THT]
  R7 = Resistor [tolerance=±5% resistance=220 package=THT]
  R6 = Resistor [tolerance=±5% resistance=220 package=THT]
  R3 = Resistor [tolerance=±5% resistance=220 package=THT]
  VCC1 = Battery
  LED3 = Super Flux LED blue [color=Blue]
  ANT1 = Antenna  # not connected
  ANT2 = Antenna  # not connected
  ANT3 = Antenna
  ANT4 = Antenna

nets:
  N1: LED1.anode, LED1.cathode, LED2.cathode, LED2.anode, LED4.anode, LED4.cathode, R2.Pin_1, R4.Pin_1, R5.Pin_1, R8.Pin_0, R9.Pin_0, R7.Pin_1, R6.Pin_1, R3.Pin_1, VCC1.+, LED3.cathode, LED3.anode, ANT3.antenna_lead, ANT4.antenna_lead
  N2: R2.Pin_0, R4.Pin_0, R5.Pin_0, R8.Pin_1, R9.Pin_1, R7.Pin_0, R6.Pin_0, R3.Pin_0, VCC1.-
